# Fritzing sketch custom_light_sketch (saved by Fritzing 0.9.3b)
breadboards: 1

parts:
  Part1 = Arduino Uno (Rev3)
  LED1 = LEDs [package=led10mm]
  S1 = Round Pushbutton

nets:
  N1: Part1.5V, S1.leg1
  N2: Part1.GND, LED1.A
  N3: LED1.C, S1.leg0

custom parts:
  LEDs: LEDs Standard schematic elements and footprints for 5mm, 3mm, 1206, and 0603 sized LEDs. 5mm - Spark Fun Electronics SKU : COM-00529 (and others)
